# Fritzing sketch Curtain Sketch (saved by Fritzing 0.9.3b)
breadboards: 1

parts:
  Part1 = Arduino Leonardo (Rev3b)
  LED1 = LEDs [package=led10mm]
  LED2 = smd LED [color="Red (633nm)" package="1206 [SMD]"]
  R1 = Resistor [tolerance=±5% resistance=220 package=THT]
  R2 = Resistor [tolerance=±5% resistance=220 package="0402 [SMD]"]
  R3 = Photocell (LDR) [package=THT]
  R4 = Resistor [tolerance=±5% resistance=100k package=THT]
  J1 = Basic Servo
  S4 = Pushbutton [package="[SMD]"]
  R5 = Resistor [tolerance=±5% resistance=10k package=THT]
  U1 = SWITCH_SPDT [package=kps-1290]

nets:
  N1: Part1.D3_PWM/SCL, LED1.A
  N2: Part1.D4/A6, U1.P
  N3: Part1.D5_PWM, LED2.anode
  N4: Part1.D7, S4.Pin_3, S4.Pin_4, R5.Pin_1
  5V: Part1.5V, R3.pin_0, J1.vcc, R5.Pin_0, U1.S
  GND: Part1.GND, R1.Pin_0, R2.Pin_0, R4.Pin_1, J1.gnd, S4.Pin_1, S4.Pin_2, U1.O
  N5: Part1.A0, R3.pin_1, R4.Pin_0
  N6: LED1.C, R2.Pin_1
  N7: LED2.cathode, R1.Pin_1
